// Logisim project IT012_LAB01_25520646.circ as structural Verilog: 1 circuit, main circuit Warmup
module Warmup (
  input  A,
  input  B,
  output F
);

  wire not_1_out;

  not not_1 (not_1_out, B);
  and and_1 (F, A, not_1_out);
endmodule
